# Fritzing sketch my_garage (saved by Fritzing 0.9.3b)
breadboards: 1

parts:
  Nano1 = Arduino Nano (Rev3.0)
  DHT2 = DHT11 Humitidy and Temperature Sensor
  R3 = Resistor [tolerance=±5% resistance=10k package=THT]
  Relay_for_vent = Keyes Relay [package=THT]
  Relay_for_hotter = Keyes Relay [package=THT]
  common_socket = Lilypad Battery Connect
  Socket_vent = Lilypad Battery Connect
  Socket_hotter = Lilypad Battery Connect

nets:
  GND: Nano1.GND, DHT2.GND, R3.Pin_1, Relay_for_vent.power, Relay_for_hotter.power
  N1: Nano1.D2, Relay_for_hotter.ground
  N2: Nano1.D3, Relay_for_vent.ground
  N3: Nano1.D8, DHT2.DATA, R3.Pin_0
  5V: Nano1.5V, DHT2.VDD, Relay_for_hotter.signal
  N4: Relay_for_vent.C, Relay_for_hotter.C, common_socket.+
  N5: Relay_for_vent.NO, Socket_vent.-
  N6: Relay_for_hotter.NO, Socket_hotter.-
  N7: common_socket.-, Socket_vent.+, Socket_hotter.+

notes:
  240V AC power supply

custom parts:
  DHT11 Humitidy and Temperature Sensor: DHT11 Humidity and Temperature Sensor
  Keyes Relay: The Keyes 5V relay module is suitable for SCM development, home appliance control. It uses a 5V~12V TIL control signal which can control DC / AC signal.

// code stored in the sketch: my_garage.ino
#include <DHT.h>
#include <DHT_U.h>

/*####################################################################
 BOARD -> ARDUINO NANO
 sensor www.microbot.it temp+humidity 
 * +5V   -> 5V
 * GND   -> GND
 * DATA  -> digital pin 8

#######################################################################*/

//switch on vent on 
int humidity_on = 80;
//switch off vent on 
int humidity_off = 40;
//switch on hotter on 
int temper_on = 4;
//switch off hotter on 
int temper_off = 8;
unsigned int gettemp=0;

#include <SimpleDHT.h>
int pinDHT11 = 8;
SimpleDHT11 dht11(pinDHT11);

#define RELAY_HOT 2
#define RELAY_VENT 3
int states [RELAY_VENT+1] = {HIGH, HIGH,HIGH, HIGH};

void setup()
{
  pinMode(RELAY_VENT, OUTPUT); 
  pinMode(RELAY_HOT, OUTPUT);
    relayOn(RELAY_VENT);
    relayOn(RELAY_HOT);
  
  Serial.begin(9600);
  delay(1000);          // wait for sensor initialization
    while(!Serial){
      ; // wait for serial port to connect. Needed for native USB port only
    }

  Serial.println("\n[memCheck]");
  Serial.println(freeRam());

    relayOff(RELAY_VENT);
    relayOff(RELAY_HOT);
}

void loop()
{
   // ???????? ?????? 60 ????
   if(millis()/60000!=gettemp) {  
    gettemp=millis()/60000;
    //log(readDHT());
    if(gettemp %2 == 0) {
      checkHumidity();
    }
    else {
      checkTemper();
    }
   }
}

void readTemp(){
 Serial.println("=================================");
  Serial.println("Sample DHT11...");
  
  // read without samples.
  byte temperature = 0;
  byte humidity = 0;
  int err = SimpleDHTErrSuccess;
  if ((err = dht11.read(&temperature, &humidity, NULL)) != SimpleDHTErrSuccess) {
    Serial.print("Read DHT11 failed, err="); Serial.println(err);delay(1000);
    return;
  }
  
  Serial.print("Sample OK: ");
  Serial.print((int)temperature); Serial.print(" *C, "); 
  Serial.print((int)humidity); Serial.println(" H");
  
  // DHT11 sampling rate is 1HZ.
}
void relayOn(int relay){
  if(states[relay] != LOW){
    digitalWrite(relay, LOW);  // ???????? ????
    states[relay] = LOW;
    String msg = String("relay switch on ");
    msg += relay;
    Serial.println(msg);
    log(msg);
  }
}

void relayOff(int relay){
  if(states[relay] != HIGH){
    digitalWrite(relay, HIGH);  // ????????? ????
    states[relay] = HIGH;
    String msg = String("relay switch off ");
    msg += relay;
    log(msg);
  }
}

void log(String msg){
       //File myFile = SD.open("temper.log", FILE_WRITE);
       String record="";//get_time();
       record+=(" " + msg);
       Serial.println(record);
       //myFile.println(record);
       //myFile.close();
}

 
int getHumidity(){
  // Reading temperature or humidity takes about 250 milliseconds!
  // Sensor readings may also be up to 2 seconds 'old' (its a very slow sensor)
  byte temp;
  byte hum;
  if(dht11.read(DHTPIN, &temp, &hum, NULL)){
    log("can't get humidity and temperature");
    return 0;
  }
  String msg = String("humidity is ");
  //************** DEBUG ONLY
  hum = random(40)+60;
  msg += hum;
  log(msg);
  return hum;
}

int getTemper(){
  // Reading temperature or humidity takes about 250 milliseconds!
  // Sensor readings may also be up to 2 seconds 'old' (its a very slow sensor)
  byte temp;
  byte hum;
  if(dht11.read(DHTPIN, &temp, &hum, NULL)){
    log("can't get humidity and temperature");
    return 100;
  }
  String msg = String("temperature is ");
  //************** DEBUG ONLY
  temp = random(10);
  msg += temp;
  log(msg);
  return temp;
}
int freeRam () {
  extern int __heap_start, *__brkval; 
  int v; 
  return (int) &v - (__brkval == 0 ? (int) &__heap_start : (int) __brkval); 
}

// code stored in the sketch: nano_with_dht11.ino
#include <DHT.h>
#include <DHT_U.h>

/*####################################################################
 Kostas Tsirogiannis
 tsirogk@gmail.com
 
 I recombined two example sketches to make 
 Arduino Yun display temp and humidity to LCD (and optionally serial)
 Made from a combination of original dht11 library and the blog 
 http://www.geeetech.com/wiki/index.php/Electric_thermometer_by_using_DHT11_sensor_module
 
 BOARD -> ARDUINO YUN
 sensor www.microbot.it temp+humidity 
 * +5V   -> 5V
 * GND   -> GND
 * DATA  -> digital pin 8

 HISTORY:
 Mirko Prosseda - Original version (21/07/2013)
#######################################################################*/


//#include <LiquidCrystal.h>
#include <Adafruit_Sensor.h>
#include <DHT.h>
#include <DHT_U.h>
#define DHTTYPE           DHT11 
#define DHTPIN 8 
//LiquidCrystal lcd(12, 11, 5, 4, 3, 2);
DHT_Unified dht(DHTPIN, DHTTYPE);
void setup()

{
  Serial.begin(9600);
  Serial.println("DHT11 Humidity and Temperature Digital Sensor test sketch");
  Serial.print("LIBRARY VERSION: ");   // ??????? ?????   
Serial.println(DHT11LIB_VERSION);   
Serial.println();                    // ?????? ??????
  delay(1000);          // wait for sensor initialization
//lcd.begin(16, 2);
}

void loop()
{
Serial.print("Sensor status: ");
readTemp();

  delay(2500);
}

void readTemp(){
 // Get temperature event and print its value.
  sensors_event_t event;  
  dht.temperature().getEvent(&event);
  if (isnan(event.temperature)) {
    Serial.println("Error reading temperature!");
  }
  else {
    Serial.print("Temperature: ");
    Serial.print(event.temperature);
    Serial.println(" *C");
  }
  // Get humidity event and print its value.
  dht.humidity().getEvent(&event);
  if (isnan(event.relative_humidity)) {
    Serial.println("Error reading humidity!");
  }
  else {
    Serial.print("Humidity: ");
    Serial.print(event.relative_humidity);
    Serial.println("%");
  }
}
